// Logisim project ALU.circ as structural Verilog: 1 circuit, main circuit main
module main (
  input  CS2,
  input  CS1,
  input  CS0,
  input  A0,
  input  A1,
  input  B0,
  input  B1,
  input  B2,
  input  A2,
  input  B3,
  input  A3,
  output Cin,
  output F3,
  output S,
  output F2,
  output S1,
  output en2,
  output en1,
  output C,
  output S2,
  output F1,
  output V,
  output Z,
  output F0
);

  wire n7404_1_p2, n7404_1_p3, n7404_1_p6, n7404_1_p7, n7404_1_p10, n7404_2_p2, n7404_2_p4, n7404_2_p7,
       n7408_1_p2, n7408_1_p3, n7408_1_p8, n7432_1_p8, n7432_2_p2, n7486_1_p2, n7486_1_p6, n7486_1_p7,
       n7486_2_p1, n7486_2_p2, n7486_2_p7, n74157_1_p2, n74157_1_p3, n74157_1_p8, n74157_1_p9, n74157_2_p2,
       n74157_2_p3, n74157_2_p8, n74157_2_p9;

  // _7404 7404_1: pin names not known; wires that end beside it: 1'b0, n7404_1_p2, n7404_1_p3, B0, CS2, n7404_1_p6, n7404_1_p7, B1, CS1, n7404_1_p10, CS0, 1'b1
  // _74157 74157_1: pin names not known; wires that end beside it: 1'b0, n74157_1_p2, n74157_1_p3, 1'b1, 1'b1, B2, B1, n74157_1_p8, n74157_1_p9, 1'b1, 1'b1, B3, B0, en1, CS1, 1'b1
  // _7404 7404_2: pin names not known; wires that end beside it: 1'b0, n7404_2_p2, B3, n7404_2_p4, B2, Z, n7404_2_p7, 1'b1
  // _7408 7408_1: pin names not known; wires that end beside it: 1'b0, n7408_1_p2, n7408_1_p3, CS2, n7404_1_p3, n7404_1_p10, n7404_1_p10, n7408_1_p8, n7404_1_p7, CS0, 1'b1
  // _7486 7486_1: pin names not known; wires that end beside it: 1'b0, n7486_1_p2, A2, n74157_1_p2, V, n7486_1_p6, n7486_1_p7, A3, C, n74157_1_p8, 1'b1
  // _7486 7486_2: pin names not known; wires that end beside it: n7486_2_p1, n7486_2_p2, A0, CS2, n74157_1_p9, CS1, n7486_2_p7, A1, n74157_1_p3, 1'b1
  // _74157 74157_2: pin names not known; wires that end beside it: 1'b0, n74157_2_p2, n74157_2_p3, n7404_2_p4, n7404_1_p6, B2, B1, n74157_2_p8, n74157_2_p9, n7404_2_p2, n7404_1_p2, B3, B0, en2, CS1, 1'b1
  // _7432 7432_1: pin names not known; wires that end beside it: 1'b0, Cin, en2, CS1, n7408_1_p8, n7408_1_p2, CS2, n7432_1_p8, en1, F0, n7408_1_p3, F1, n7486_2_p2, 1'b1
  // _7483 7483_1: pin names not known; wires that end beside it: n7486_2_p7, F0, n74157_2_p3, n7486_2_p1, F1, n74157_2_p9, 1'b1, 1'b0, n74157_2_p2, Cin, n7486_1_p2, F2, n7486_1_p7, 1'b0, 1'b0
  // _7432 7432_2: pin names not known; wires that end beside it: 1'b0, n7432_2_p2, n7404_2_p7, F2, n7432_1_p8, F3, n7432_2_p2, 1'b1
  // _7483 7483_2: pin names not known; wires that end beside it: 1'b0, F3, 1'b0, n7486_1_p6, C, n74157_2_p8, 1'b1, 1'b0, 1'b0, n7486_1_p7, 1'b0, 1'b0, 1'b0

  assign S = F3;
  assign S1 = CS1;
  assign S2 = CS1;
endmodule
